# Fritzing sketch sketch (saved by Fritzing 0.8.7b)
breadboards: 1

parts:
  Part1 = Arduino Uno (Rev3) - ICSP
  J1 = Piezo Speaker
  RHT1 = Humidity and Temperature Sensor RHT03
  R1 = Resistor [tolerance=±5% resistance=10k package=THT]
  Part2 = SRF05 Ultrasonic Rangefinder
  Part3 = Bluetooth HC-05 Macho
  R3 = Resistor [tolerance=±5% resistance=1k package=THT]
  R4 = Resistor [tolerance=±5% resistance=1k package=THT]
  R5 = PHOTOCELL [package=photocell-kit]
  R6 = Resistor [tolerance=±5% resistance=560 package=THT]

nets:
  N1: Part1.A0, R5.P$1, R6.Pin_0
  VCC: Part1.5V, RHT1.Vcc, R1.Pin_0, Part2.VCC, Part3.VCC, R5.P$2
  N2: Part1.D8, Part3.TXD
  N3: Part1.D9_PWM, J1.pin2
  N4: Part1.D3_PWM, RHT1.Data-signal, R1.Pin_1
  N5: Part1.D5_PWM, Part2.Trig
  N6: Part1.D6_PWM, Part2.Echo
  N7: Part1.D7, R3.Pin_0
  GND: Part1.GND, J1.pin1, RHT1.GND_2, Part2.GND, Part3.GND, R4.Pin_1, R6.Pin_1
  N8: Part3.RXD, R3.Pin_1, R4.Pin_0
